# Fritzing sketch Plant_Watering_System (saved by Fritzing 0.9.2b)
circuit board: 8.46667cm x 5.64444cm
breadboards: 1

parts:
  Part1 = Arduino Uno (Rev3) - ICSP
  Part3 = Memoire 1.0 - SD card log shield
  DHT1 = DHT11 Humitidy and Temperature Sensor [part_number=DHT11]
  VALVE1 = Plastic Solenoid Valve
  LED1 = LED - 5mm [color="Red (633nm)" package="5 mm [THT]"]
  Part4 = FC-28 Soil Hygrometer Module
  Part5 = FC-28 Soil Hygrometer Module - Probe
  Q2 = Basic FET N-Channel [package="TO220 [THT]"]
  D1 = Zener Diode [part_number=1N4732A breakdown_voltage=3.6V package="300 mil [THT]"]
  R1 = Resistor [tolerance=±5% resistance=220 package=THT]
  S1 = Pushbutton [package=THT]
  Part8 = Lithium Ion Battery Pack 3.7V 4400mAh [part_number=354]
  Part9 = Lithium Ion Battery Pack 3.7V 4400mAh [part_number=354]
  Part10 = Lithium Ion Battery Pack 3.7V 6600mAh [part_number=353]
  Part11 = Lithium Ion Battery Pack 3.7V 6600mAh [part_number=353]
  Part12 = Lithium Ion Battery Pack 3.7V 6600mAh [part_number=353]

nets:
  N1: Part1.A1, Part3.A_IN_1, Part4.VCC
  GND: Part1.GND, Part3.GND, DHT1.GND, LED1.cathode, Part4.GND, Q2.source, R1.Pin_0, Part8.negative, Part12.negative
  N2: Part1.D11_PWM/MOSI, Part3.DIG_11, DHT1.DATA
  N3: Part1.D12/MISO, Part3.DIG_12, R1.Pin_1, S1.leg0
  N4: Part1.D13/SCK, Part3.DIG_13, LED1.anode
  N5: Part1.D4, Part3.DIG_4, Q2.gate
  N6: Part1.D6_PWM, Part3.DIG_6, Part4.DO
  VIN: Part1.VIN, Part3.VIN, DHT1.VDD, VALVE1.no_name_yet#1, D1.cathode, S1.leg1, Part9.positive, Part10.positive
  N7: VALVE1.no_name_yet#2, Q2.drain, D1.anode
  N8: Part4.POS, Part5.POS
  N9: Part4.NEG, Part5.NEG
  N10: Part8.positive, Part9.negative
  N11: Part10.negative, Part11.positive
  N12: Part11.negative, Part12.positive

notes:
  7.4V battery pack built with 2 x 3.7V, in series, to power Arduino.
  I used a USB battery back.
  12V battery pack built with 3 x 3.7V, in series, to drive the valve.
  I used a 12V lithium battery pack.

custom parts:
  DHT11 Humitidy and Temperature Sensor: DHT11 Humidity and Temperature Sensor
  FC-28 Soil Hygrometer Module: The FC-28 is a soil hygrometer module that uses the Texas Instruments LM393 comparator chip to provide an analog measurement of soil humidity. The digital output is high when soil moisture is over a certain threshold, as determined by adjusting the potentiometer.
  FC-28 Soil Hygrometer Module - Probe: The FC-28 is a soil hygrometer module that uses the Texas Instruments LM393 comparator chip to provide an analog measurement of soil humidity.
  Lithium Ion Battery Pack 3.7V 4400mAh: This lithium ion pack is made of 2 balanced 2200mAh cells for a total of 4400mA capacity! The cells are connected in parallel and spot-welded to a protection circuit that provides over-voltage, under-voltage and over-current protection. Each cell can provide 1A of current for about 4 hours so all together the peak current you can draw is a little over 1.5 Amps. Note that these batteries are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
  Lithium Ion Battery Pack 3.7V 6600mAh: This lithium ion pack is made of 3 balanced 2200mAh cells for a total of 6600mA capacity! The cells are connected in parallel and spot-welded to a protection circuit that provides over-voltage, under-voltage and over-current protection. Each cell can provide 0.5C of current (1.1 A per) so all together the peak current you can draw is over 3.3 Amps. Note that these batteries are not designed to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
